// Logisim project Digital 8.circ as structural Verilog: 1 circuit, main circuit main
module main (
  input  VCC
);

  wire and_1_out, and_2_out, and_3_out, and_4_out, not_1_out, not_2_out, not_3_out, or_1_out, or_2_out,
       or_3_out, or_4_out;

  not not_1 (not_1_out, 1'b0);
  not not_2 (not_2_out, 1'b0);
  not not_3 (not_3_out, 1'b0);
  and and_1 (and_1_out, not_3_out, 1'b0);
  and and_2 (and_2_out, not_2_out, 1'b0);
  and and_3 (and_3_out, not_2_out, not_3_out);
  and and_4 (and_4_out, not_1_out, 1'b0, 1'b0);
  or or_1 (or_1_out, and_1_out, 1'b0);
  or or_2 (or_2_out, or_1_out, and_2_out);
  or or_3 (or_3_out, or_2_out, and_3_out);
  or or_4 (or_4_out, or_2_out, and_4_out);
  _7_Segment_Display u_7_segment_display_1 (.c(or_4_out), .dp(1'b0));  // open: g, f, a, b, e, d
endmodule
