// Logisim project Multiplexor y demultiplexor.circ as structural Verilog: 1 circuit, main circuit main
module main (
  input  [2:0] _0,
  input  [2:0] in_2,
  input  [2:0] in_3,
  input  [2:0] in_4,
  input  [2:0] in_5,
  input  [2:0] in_6,
  input  [2:0] in_7,
  input  [2:0] _7,
  input  [2:0] in_9,
  input  in_10,
  output [2:0] out_11,
  output [2:0] _0_2,
  output [2:0] out_13,
  output [2:0] out_14,
  output [2:0] out_15,
  output [2:0] out_16,
  output [2:0] out_17,
  output [2:0] out_18,
  output [2:0] _7_2
);

  Demultiplexer #(.select(3), .width(3)) demultiplexer_1 (
    .out0(_0_2), .out1(out_13), .out2(out_14), .out3(out_15), .out4(out_16), .out5(out_17), .out6(out_18),
    .out7(_7_2), .in(in_9), .sel(3'b001), .en(in_10));
  Multiplexer #(.select(3), .width(3)) multiplexer_1 (
    .in0(_0), .in1(in_2), .in2(in_3), .in3(in_4), .in4(in_5), .in5(in_6), .in6(in_7), .in7(_7), .out(out_11),
    .sel(3'b111));  // open: en

  // Notes on the sheet:
  //   Benjamin Martinez Jeldres
endmodule
