// Logisim project Subcircuito sumador1-bit.circ as structural Verilog: 1 circuit, main circuit main
module main (
  input  [3:0] in_1,
  input  [3:0] in_2,
  input  [3:0] in_3,
  output [3:0] out_4,
  output [3:0] out_5
);

  wire [3:0] and_1_out, and_2_out, xor_1_out;

  assign xor_1_out = in_1 ^ in_2;  // XOR_Gate xor_1, 4 bits wide
  assign and_1_out = in_1 & in_2;  // AND_Gate and_1, 4 bits wide
  assign out_4 = xor_1_out ^ in_3;  // XOR_Gate xor_2, 4 bits wide
  assign and_2_out = xor_1_out & in_3;  // AND_Gate and_2, 4 bits wide
  assign out_5 = and_2_out | and_1_out;  // OR_Gate or_1, 4 bits wide
endmodule
