// Logisim project Subcircuito.circ as structural Verilog: 1 circuit, main circuit main
module main (
  input  in_1,
  input  in_2,
  input  in_3,
  input  in_4,
  input  in_5,
  input  in_6,
  output out_7
);

  wire [1:0] multiplexer_1_out, multiplexer_2_out;
  wire [1:1] multiplexer_3_out, undriven, undriven_2, undriven_3, undriven_4;

  Multiplexer #(.width(2)) multiplexer_1 (
    .in0({undriven[1], in_1}), .in1({undriven_2[1], in_2}), .out(multiplexer_1_out), .sel(in_6));  // open: en
  Multiplexer #(.width(2)) multiplexer_2 (
    .in0({undriven_3[1], in_3}), .in1({undriven_4[1], in_4}), .out(multiplexer_2_out), .sel(in_6));  // open: en
  Multiplexer #(.width(2)) multiplexer_3 (
    .in0(multiplexer_1_out), .in1(multiplexer_2_out), .out({multiplexer_3_out[1], out_7}), .sel(in_5));  // open: en
  // Pins of 1 and 2 bits meet at {multiplexer_3_out[1], out_7}
  // Pins of 1 and 2 bits meet at {undriven_4[1], in_4}
  // Pins of 1 and 2 bits meet at {undriven[1], in_1}
  // Pins of 1 and 2 bits meet at {undriven_3[1], in_3}
  // Pins of 1 and 2 bits meet at {undriven_2[1], in_2}
endmodule
