// Logisim project numeros primos.circ as structural Verilog
module numeros_primos (
  input  A,
  input  B,
  input  C,
  input  D,
  output out_5
);

  wire and_1_out, and_2_out, and_3_out, and_4_out, not_1_out, not_2_out, not_3_out, or_1_out, or_2_out;

  not not_1 (not_1_out, A);
  not not_2 (not_2_out, B);
  not not_3 (not_3_out, C);
  and and_1 (and_1_out, not_2_out, not_2_out, C);
  or or_1 (or_1_out, not_1_out, D);
  or or_2 (or_2_out, not_1_out, not_3_out);
  and and_2 (and_2_out, and_1_out, or_1_out);
  and and_3 (and_3_out, B, D);
  and and_4 (and_4_out, or_2_out, and_3_out);
  or or_3 (out_5, and_4_out, and_2_out);

  // Notes on the sheet:
  //   Numeros primos
  //   Benjamin Martinez Jeldres
endmodule
